// Logisim project ttt_wkt.circ as structural Verilog: 1 circuit, main circuit main
module main (
);

  wire button_1_out, button_2_out, button_3_out, button_4_out, button_5_out, button_6_out, button_7_out,
       button_8_out, button_9_out, clock_1_out, clock_2_out, Reset_out;
  wire [7:0] rom_1_data;
  wire [8:0] demultiplexer_1_out1, Omoves, Xmoves;

  Button button_1 (.out(button_1_out));
  Button button_2 (.out(button_2_out));
  Button button_3 (.out(button_3_out));
  Button button_4 (.out(button_4_out));
  Button button_5 (.out(button_5_out));
  Button button_6 (.out(button_6_out));
  Button button_7 (.out(button_7_out));
  Button button_8 (.out(button_8_out));
  Button button_9 (.out(button_9_out));
  Button Reset (.out(Reset_out));
  Clock clock_1 (.out(clock_1_out));
  // Probe on Omoves
  // Probe on Xmoves
  LED led_1 (.in(Omoves[0]));
  J_K_Flip_Flop j_k_ff_1 (
    .J(button_1_out), .clk(clock_1_out), .K(Xmoves[0]), .Q(Omoves[0]), .reset(Reset_out));  // open: Qn, preset, en
  LED led_2 (.in(Omoves[1]));
  J_K_Flip_Flop j_k_ff_2 (
    .J(button_2_out), .clk(clock_1_out), .K(Xmoves[1]), .Q(Omoves[1]), .reset(Reset_out));  // open: Qn, preset, en
  LED led_3 (.in(Omoves[2]));
  J_K_Flip_Flop j_k_ff_3 (
    .J(button_3_out), .clk(clock_1_out), .K(Xmoves[2]), .Q(Omoves[2]), .reset(Reset_out));  // open: Qn, preset, en
  LED led_4 (.in(Omoves[3]));
  J_K_Flip_Flop j_k_ff_4 (
    .J(button_4_out), .clk(clock_1_out), .K(Xmoves[3]), .Q(Omoves[3]), .reset(Reset_out));  // open: Qn, preset, en
  LED led_5 (.in(Omoves[4]));
  J_K_Flip_Flop j_k_ff_5 (
    .J(button_5_out), .clk(clock_1_out), .K(Xmoves[4]), .Q(Omoves[4]), .reset(Reset_out));  // open: Qn, preset, en
  LED led_6 (.in(Omoves[5]));
  J_K_Flip_Flop j_k_ff_6 (
    .J(button_6_out), .clk(clock_1_out), .K(Xmoves[5]), .Q(Omoves[5]), .reset(Reset_out));  // open: Qn, preset, en
  LED led_7 (.in(Omoves[6]));
  J_K_Flip_Flop j_k_ff_7 (
    .J(button_7_out), .clk(clock_1_out), .K(Xmoves[6]), .Q(Omoves[6]), .reset(Reset_out));  // open: Qn, preset, en
  LED led_8 (.in(Omoves[7]));
  J_K_Flip_Flop j_k_ff_8 (
    .J(button_8_out), .clk(clock_1_out), .K(Xmoves[7]), .Q(Omoves[7]), .reset(Reset_out));  // open: Qn, preset, en
  LED led_9 (.in(Omoves[8]));
  J_K_Flip_Flop j_k_ff_9 (
    .J(button_9_out), .clk(clock_1_out), .K(Xmoves[8]), .Q(Omoves[8]), .reset(Reset_out));  // open: Qn, preset, en
  // Probe on {Xmoves, Omoves}
  ROM #(.addrWidth(18)) rom_1 (.addr({Xmoves, Omoves}), .data(rom_1_data));  // open: sel
  Clock clock_2 (.out(clock_2_out));
  LED Tie (.in(rom_1_data[4]));
  LED Win (.in(rom_1_data[5]));
  LED led_10 (.in(Xmoves[0]));
  J_K_Flip_Flop j_k_ff_10 (
    .J(demultiplexer_1_out1[0]), .clk(clock_2_out), .K(1'b0), .Q(Xmoves[0]), .reset(Reset_out));  // open: Qn, preset, en
  LED led_11 (.in(Xmoves[1]));
  J_K_Flip_Flop j_k_ff_11 (
    .J(demultiplexer_1_out1[1]), .clk(clock_2_out), .K(1'b0), .Q(Xmoves[1]), .reset(Reset_out));  // open: Qn, preset, en
  LED led_12 (.in(Xmoves[2]));
  J_K_Flip_Flop j_k_ff_12 (
    .J(demultiplexer_1_out1[2]), .clk(clock_2_out), .K(1'b0), .Q(Xmoves[2]), .reset(Reset_out));  // open: Qn, preset, en
  LED led_13 (.in(Xmoves[3]));
  J_K_Flip_Flop j_k_ff_13 (
    .J(demultiplexer_1_out1[3]), .clk(clock_2_out), .K(1'b0), .Q(Xmoves[3]), .reset(Reset_out));  // open: Qn, preset, en
  LED led_14 (.in(Xmoves[4]));
  J_K_Flip_Flop j_k_ff_14 (
    .J(demultiplexer_1_out1[4]), .clk(clock_2_out), .K(1'b0), .Q(Xmoves[4]), .reset(Reset_out));  // open: Qn, preset, en
  LED led_15 (.in(Xmoves[5]));
  J_K_Flip_Flop j_k_ff_15 (
    .J(demultiplexer_1_out1[5]), .clk(clock_2_out), .K(1'b0), .Q(Xmoves[5]), .reset(Reset_out));  // open: Qn, preset, en
  LED led_16 (.in(Xmoves[6]));
  J_K_Flip_Flop j_k_ff_16 (
    .J(demultiplexer_1_out1[6]), .clk(clock_2_out), .K(1'b0), .Q(Xmoves[6]), .reset(Reset_out));  // open: Qn, preset, en
  LED led_17 (.in(Xmoves[7]));
  J_K_Flip_Flop j_k_ff_17 (
    .J(demultiplexer_1_out1[7]), .clk(clock_2_out), .K(1'b0), .Q(Xmoves[7]), .reset(Reset_out));  // open: Qn, preset, en
  LED led_18 (.in(Xmoves[8]));
  J_K_Flip_Flop j_k_ff_18 (
    .J(demultiplexer_1_out1[8]), .clk(clock_2_out), .K(1'b0), .Q(Xmoves[8]), .reset(Reset_out));  // open: Qn, preset, en
  Demultiplexer #(.select(4), .enable("false")) demultiplexer_1 (
    .out1(demultiplexer_1_out1[0]), .out2(demultiplexer_1_out1[1]), .out3(demultiplexer_1_out1[2]),
    .out4(demultiplexer_1_out1[3]), .out5(demultiplexer_1_out1[4]), .out6(demultiplexer_1_out1[5]),
    .out7(demultiplexer_1_out1[6]), .out8(demultiplexer_1_out1[7]), .out9(demultiplexer_1_out1[8]),
    .in(1'b1), .sel(rom_1_data[3:0]));  // open: out0, out10, out11, out12, out13, out14, out15

  // Notes on the sheet:
  //   contents of rom_1 (hex, n*v repeats v):
  //   0 5 1 0 5 0 0 0 1 7*0 1 15*0 3 31*0 5 63*0 2 127*0 5 261*0 4 0 0 0 5 0 5 5*0 8 0 7 0 0 0 6 9*0 7 5*0
  //   5 7*0 4 17*0 5 5*0 2 7*0 3 49*0 5 5*0 3 7*0 2 113*0 5 5*0 3 7*0 3 368*0 7 0 0 7 0 0 0 7 7*0 1 15*0 7
  //   31*0 9 191*0 7 203*0 5 11*0 23 15*0 23 43*0 7 0 0 0 23 23*0 23 23*0 23 7*0 23 119*0 23 71*0 23 144*0
  //   4 4 5*0 5 7*0 4 47*0 1 63*0 1 127*0 1 305*0 8 5*0 22 9*0 5 5*0 22 7*0 22 25*0 5 13*0 22 9*0 5 5*0 22
  //   7*0 22 23*0 22 7*0 22 15*0 22 41*0 5 7*0 8 5*0 22 9*0 7 5*0 22 7*0 22 23*0 22 7*0 22 15*0 22 39*0 22
  //   7*0 22 15*0 22 695*0 20 15*0 20 7*0 20 39*0 20 15*0 20 7*0 20 23*0 20 7*0 20 15*0 20 55*0 20 15*0 20
  //   7*0 20 23*0 20 7*0 20 15*0 20 39*0 20 7*0 20 15*0 20 629*0 27 15*0 27 11*0 27 0 27 17*0 5 41*0 3
  //   21*0 5 41*0 2 85*0 6 41*0 3 899*0 27 59*0 23 191*0 23 114*0 5 13*0 9 8 46*0 5 5 13*0 1 48*0 5 5 13*0
  //   2 112*0 5 7 13*0 1 321*0 8 125*0 22 65*0 27 61*0 22 63*0 22 256*0 9 62*0 21 191*0 21 319*0 20 127*0
  //   20 63*0 20 82*0 3 0 2 1 0 0 7 0 0 1 20*0 2 0 0 9 28*0 4 1 0 2 0 0 0 1 23*0 2 32*0 4 0 0 4 59*0 9
  //   64*0 2 1 0 6 0 0 0 1 23*0 3 31*0 8 63*0 7 141*0 29 23*0 29 0 0 0 3 0 29 25*0 4 0 0 0 29 0 2 21*0 29
  //   5*0 2 29*0 4 0 0 0 3 0 29 21*0 3 5*0 2 25*0 29 5*0 29 61*0 6 0 0 0 3 0 6 21*0 3 5*0 3 25*0 8 5*0 8
  //   57*0 7 5*0 7 132*0 28 23*0 28 0 0 0 7 27*0 4 6*0 1 20*0 28 0 0 28 0 0 0 1 28*0 4 27*0 7 34*0 9 27*0
  //   9 36*0 6 0 0 0 7 23*0 3 31*0 28 0 0 28 27*0 28 32*0 7 234*0 28 63*0 29 31*0 29 27*0 23 99*0 28 27*0
  //   23 63*0 23 98*0 27 23*0 27 5*0 27 1 24*0 4 36*0 1 26*0 4 36*0 1 90*0 4 29*0 2 27 5*0 1 55*0 8 63*0
  //   27 201*0 29 63*0 27 31*0 29 23*0 29 5*0 22 65*0 27 31*0 8 23*0 8 5*0 22 33*0 27 23*0 27 5*0 22 384*0
  //   27 55*0 28 63*0 27 326*0 20 127*0 20 63*0 20 154*0 26 0 2 27*0 2 33*0 3 0 26 1 26*0 3 0 0 9 28*0 26
  //   0 0 26 124*0 26 63*0 26 0 0 26 225*0 29 63*0 27 31*0 26 127*0 26 63*0 26 222*0 28 63*0 9 31*0 26
  //   27*0 9 99*0 26 27*0 28 35*0 26 733*0 8 63*0 27 31*0 26 29*0 9 9 64*0 27 31*0 26 29*0 8 8 32*0 26
  //   29*0 27 27 2167*0 8 0 7 59*0 3 63*0 2 127*0 2 899*0 7 59*0 23 67*0 7 59*0 23 63*0 23 705*0 29 125*0
  //   22 127*0 22 895*0 20 127*0 20 63*0 20 893*0 27 47*0 25 63*0 25 3454*0 2 24 5*0 1 55*0 24 63*0 24
  //   393*0 7 55*0 24 5*0 8 57*0 24 5*0 7 384*0 28 55*0 24 63*0 24 2749*0 20 65*0 20 59*0 20 0 0 20 65*0
  //   20 58*0 20 0 0 20 60*0 20 0 0 20 321*0 20 127*0 20 63*0 20 318*0 20 127*0 20 63*0 20 829*0 20 127*0
  //   20 63*0 20 2194*0 24 5*0 6 9*0 24 0 0 0 5 7*0 24 0 24 95*0 24 13*0 24 113*0 24 13*0 3 354*0 5 0 0 0
  //   5 0 0 5 4*0 9 0 0 1 0 0 0 6 8*0 5 0 0 9 0 0 0 5 7*0 4 208*0 5 0 0 6 0 0 0 3 7*0 1 15*0 3 251*0 6
  //   23*0 24 223*0 24 0 0 0 23 23*0 23 889*0 25 7*0 24 111*0 24 486*0 25 14*0 21 8*0 25 6*0 21 7*0 21
  //   487*0 20 15*0 20 7*0 20 613*0 20 15*0 20 11*0 20 0 20 95*0 20 13*0 20 113*0 20 412*0 9 0 0 21 251*0
  //   21 259*0 20 223*0 20 27*0 20 370*0 25 14*0 21 111*0 21 399*0 20 111*0 20 1128*0 23 0 2 27*0 2 95*0
  //   23 127*0 2 119*0 23 1 0 6 0 0 0 23 23*0 23 141*0 29 123*0 23 127*0 23 91*0 24 0 0 0 23 0 6 21*0 23
  //   5*0 23 132*0 28 95*0 6 23*0 9 0 0 0 23 0 0 9 96*0 28 27*0 23 91*0 6 0 0 0 23 0 0 6 20*0 23 6*0 23
  //   610*0 20 23*0 20 5*0 20 95*0 20 152*0 20 94*0 20 6*0 20 23*0 20 265*0 20 127*0 20 95*0 20 23*0 20
  //   5*0 20 256*0 20 127*0 20 95*0 20 23*0 20 6*0 20 1277*0 20 223*0 20 1308*0 20 127*0 20 125*0 20 20
  //   2171*0 8 125*0 2 127*0 2 380*0 9 0 0 1 232*0 5 6*0 1 7*0 1 0 0 0 1 515*0 10 2937*0 20 3694*0 24 24
  //   5*0 1 513*0 10 510*0 10 3063*0 20 20 4239*0 7 0 0 0 6 23*0 4 31*0 3 191*0 3 1863*0 6 23*0 4 167*0 6
  //   23*0 4 31*0 4 1763*0 27 59*0 3 191*0 27 1280*0 9 62*0 1 191*0 1 575*0 10 1486*0 22 1 0 22 0 0 0 22
  //   23*0 22 485*0 6 0 0 0 3 0 22 21*0 3 5*0 22 164*0 20 23*0 20 59*0 20 0 0 20 220*0 20 0 0 20 0 0 0 20
  //   23*0 20 267*0 20 223*0 20 27*0 20 504*0 22 1 5*0 22 513*0 10 502*0 20 6*0 20 1788*0 20 251*0 20
  //   1025*0 10 2234*0 7 59*0 3 191*0 3 2111*0 10 6131*0 10 446*0 20 7440*0 29 23*0 24 223*0 24 3871*0 20
  //   223*0 20 27*0 20 4346*0 20 223*0 20 7696*0 10 16802*0 4 0 0 5 0 0 0 1 7*0 3 15*0 1 491*0 25 11*0 23
  //   11*0 25 0 0 0 23 7*0 23 1504*0 26 6*0 21 23*0 21 487*0 20 15*0 20 7*0 20 1492*0 5 11*0 3 15*0 3
  //   849*0 8 61*0 2 63*0 2 1087*0 10 81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
endmodule
